// Logisim project Tarea04-circuitos.circ as structural Verilog: 12 circuits, main circuit main
module main (
  input  r,
  input  g,
  input  e,
  output G_2,
  output R_2
);

  wire and_1_out, and_2_out, not_1_out, not_2_out;

  not not_1 (not_1_out, g);
  not not_2 (not_2_out, e);
  and and_1 (and_1_out, r, not_1_out, e);
  and and_2 (and_2_out, r, g, not_2_out);
  and and_3 (G_2, g, e);
  or or_1 (R_2, and_1_out, and_2_out);

  // Notes on the sheet:
  //   Semaforo
endmodule

module _1_a (
  input  p,
  input  q,
  output out_3
);

  wire not_1_out, not_2_out;

  not not_1 (not_1_out, p);
  not not_2 (not_2_out, q);
  or or_1 (out_3, not_1_out, not_2_out);
endmodule

module _1_b (
  input  p,
  input  q,
  output S
);


  assign S = 1'b1;
endmodule

module _1_c (
  input  p,
  input  q,
  input  r,
  output S
);

  wire not_1_out;

  not not_1 (not_1_out, r);
  or or_1 (S, not_1_out, q);
endmodule

module _1_d (
  input  p,
  input  q,
  input  r,
  output S
);


  assign S = 1'b1;
endmodule

module NAND_circuits (
  input  Y,
  input  X,
  input  X_2,
  input  Y_2,
  input  X_3,
  output S,
  output out_7,
  output out_8
);

  wire nand_1_out, nand_2_out, nand_3_out, nand_4_out;

  nand nand_1 (nand_1_out, Y, Y);
  nand nand_2 (nand_2_out, X, X);
  nand nand_3 (nand_3_out, Y_2, X_3);
  nand nand_4 (nand_4_out, Y_2, X_3);
  nand nand_5 (S, nand_1_out, nand_2_out);
  nand nand_6 (out_8, nand_3_out, nand_4_out);
  nand nand_7 (out_7, X_2, X_2);

  // Notes on the sheet:
  //   OR
  //   AND
  //   NOT
endmodule

module Semisumador_1bit (
  input  X,
  input  Y,
  input  C,
  output Resultado,
  output Acarreo
);

  wire and_1_out, and_2_out, xor_1_out;

  xor xor_1 (xor_1_out, X, Y);
  and and_1 (and_1_out, X, Y);
  xor xor_2 (Resultado, xor_1_out, C);
  and and_2 (and_2_out, xor_1_out, C);
  or or_1 (Acarreo, and_2_out, and_1_out);
endmodule

module Semisumado_4bits (
  input  [3:0] X,
  input  _0,
  input  _1,
  input  _2,
  input  _3,
  output [3:0] Salida,
  output Acarreo
);

  wire semisumador_1bit_1_acarreo, semisumador_1bit_2_acarreo, semisumador_1bit_3_acarreo;

  Semisumador_1bit semisumador_1bit_1 (
    .X(X[0]), .Y(_0), .C(1'b0), .Resultado(Salida[0]), .Acarreo(semisumador_1bit_1_acarreo));
  Semisumador_1bit semisumador_1bit_2 (
    .X(X[2]), .Y(_2), .C(semisumador_1bit_3_acarreo), .Resultado(Salida[2]),
    .Acarreo(semisumador_1bit_2_acarreo));
  Semisumador_1bit semisumador_1bit_3 (
    .X(X[1]), .Y(_1), .C(semisumador_1bit_1_acarreo), .Resultado(Salida[1]),
    .Acarreo(semisumador_1bit_3_acarreo));
  Semisumador_1bit semisumador_1bit_4 (
    .X(X[3]), .Y(_3), .C(semisumador_1bit_2_acarreo), .Resultado(Salida[3]), .Acarreo(Acarreo));
endmodule

module _10_Mult (
  input  [3:0] Z,
  input  [3:0] Y,
  output [3:0] X,
  output Acarreo,
  output Overflow
);

  Semisumado_4bits semisumado_4bits_1 (
    .X(Z), .Salida(X), .Acarreo(Acarreo), ._0(1'b0), ._1(Y[0]), ._3(Y[2]), ._2(Y[1]));

  assign Overflow = Y[3];

  // Notes on the sheet:
  //   X=2Y+Z
endmodule

module Circ4_Motor (
  input  A,
  input  N,
  input  T,
  output Motor,
  output Lampara
);

  wire and_1_out, and_2_out, and_3_out, not_1_out, not_2_out, not_3_out, or_1_out;

  not not_1 (not_1_out, A);
  not not_2 (not_2_out, T);
  and and_1 (and_1_out, not_1_out, N);
  not not_3 (not_3_out, N);
  and and_2 (and_2_out, A, N);
  or or_1 (or_1_out, not_2_out, and_1_out);
  and and_3 (and_3_out, A, not_3_out);
  or or_2 (Lampara, T, and_2_out);
  or or_3 (Motor, or_1_out, and_3_out);
endmodule

module Circ4_Lampara (
  input  A,
  input  N,
  input  T,
  output Lampara
);

  wire and_1_out;

  and and_1 (and_1_out, A, N);
  or or_1 (Lampara, T, and_1_out);
endmodule

module Circ5_a (
  input  X0,
  input  X1,
  input  X2,
  output S
);

  wire and_1_out, and_2_out, not_1_out, not_2_out;

  not not_1 (not_1_out, X0);
  not not_2 (not_2_out, X1);
  and and_1 (and_1_out, X0, X1);
  and and_2 (and_2_out, not_1_out, not_2_out);
  or or_1 (S, and_1_out, and_2_out);

  // Notes on the sheet:
  //   Circ5-1
endmodule
